// Logisim project lnvk8.circ as structural Verilog: 3 circuits, main circuit main
module main (
);

  alu alu_1 ();  // open: flag_c_in, flag_s_in, flag_z_in, operation, input_a, input_b, flag_c, flag_s, flag_z, result
endmodule

module alu (
  input  flag_c_in,
  input  flag_s_in,
  input  flag_z_in,
  input  [3:0] operation,
  input  [7:0] input_a,
  input  [7:0] input_b,
  output flag_c,
  output flag_s,
  output flag_z,
  output [7:0] result
);

  wire adder_1_cout, and_1_out, not_2_out, or_1_out, subtractor_1_bout;
  wire [7:0] adder_1_out, and_2_out, multiplexer_1_out, not_1_out, or_2_out, shifter_1_out, shifter_2_out,
       subtractor_1_out, xor_1_out;

  and and_1 (and_1_out, flag_c_in, operation[2]);
  Multiplexer #(.width(8)) multiplexer_1 (.in0({8{1'b0}}), .in1(input_b), .out(multiplexer_1_out), .sel(operation[3]));
  or or_1 (or_1_out, and_1_out, operation[1]);
  Adder adder_1 (.a(input_a), .b(multiplexer_1_out), .out(adder_1_out), .cin(or_1_out), .cout(adder_1_cout));
  Subtractor subtractor_1 (
    .a(input_a), .b(multiplexer_1_out), .out(subtractor_1_out), .bin(or_1_out), .bout(subtractor_1_bout));
  Shifter shifter_1 (.in(input_a), .\dist (3'b001), .out(shifter_1_out));
  Shifter #(.shift("lr")) shifter_2 (.in(input_a), .\dist (3'b001), .out(shifter_2_out));
  assign not_1_out = ~input_a;  // NOT_Gate not_1, 8 bits wide
  assign or_2_out = input_a | multiplexer_1_out;  // OR_Gate or_2, 8 bits wide
  assign xor_1_out = input_a ^ multiplexer_1_out;  // XOR_Gate xor_1, 8 bits wide
  assign and_2_out = input_a & multiplexer_1_out;  // AND_Gate and_2, 8 bits wide
  not not_2 (not_2_out, subtractor_1_bout);
  Multiplexer #(.select(4)) multiplexer_2 (
    .in0(input_a[7]), .in1(input_a[0]), .in2(flag_c_in), .in3(flag_c_in), .in4(flag_c_in), .in5(1'b0),
    .in6(1'b0), .in7(1'b0), .in8(adder_1_cout), .in9(not_2_out), .in10(1'b0), .in11(1'b0),
    .in12(adder_1_cout), .in13(not_2_out), .in14(1'b0), .in15(not_2_out), .out(flag_c), .sel(operation));
  Multiplexer #(.select(4), .width(8)) multiplexer_3 (
    .in0(shifter_1_out), .in1(shifter_2_out), .in2(adder_1_out), .in3(subtractor_1_out), .in4(not_1_out),
    .in5({8{1'b0}}), .in6({8{1'b0}}), .in7({8{1'b0}}), .in8(adder_1_out), .in9(subtractor_1_out),
    .in10(or_2_out), .in11(xor_1_out), .in12(adder_1_out), .in13(subtractor_1_out), .in14(and_2_out),
    .in15({8{1'b0}}), .out({flag_s, result[6:0]}), .sel(operation));
  nor nor_1 (flag_z, result[0], result[1], result[2], result[3], result[4], result[5], result[6], flag_s);

  assign result[7] = flag_s;
endmodule

module alu_test (
);

  wire and_1_out, button_1_out, clock_1_out, comparator_1_eq, comparator_2_eq, comparator_3_eq, xor_1_out;
  wire [2:0] alu_1_flag_s;
  wire [7:0] alu_1_result, counter_1_q, rom_1_data;
  wire [63:8] rom_1_data_2;

  Counter counter_1 (
    .count(and_1_out), .Q(counter_1_q), .clk(xor_1_out), .clr(comparator_1_eq));  // open: load, D, carry, up
  xor xor_1 (xor_1_out, button_1_out, clock_1_out);
  Clock clock_1 (.out(clock_1_out));
  Button button_1 (.out(button_1_out));
  ROM #(.dataWidth(64)) rom_1 (.addr(counter_1_q), .data({rom_1_data_2, rom_1_data}));
  Comparator comparator_1 (.a({8{1'b1}}), .b(rom_1_data), .eq(comparator_1_eq));  // open: gt, lt
  // Probe on rom_1_data
  // Probe on rom_1_data_2[23:16]
  // Probe on rom_1_data_2[15:8]
  // Probe on alu_1_result
  and and_1 (and_1_out, comparator_2_eq, comparator_3_eq);
  Comparator comparator_2 (.a(rom_1_data_2[23:16]), .b(alu_1_result), .eq(comparator_2_eq));  // open: gt, lt
  alu alu_1 (
    .flag_c_in(rom_1_data_2[26]), .flag_s_in(rom_1_data_2[24]), .flag_z_in(rom_1_data_2[25]),
    .operation(rom_1_data_2[53:50]), .input_a(rom_1_data_2[47:40]), .input_b(rom_1_data_2[39:32]),
    .flag_c(alu_1_flag_s[2]), .flag_s(alu_1_flag_s[0]), .flag_z(alu_1_flag_s[1]), .result(alu_1_result));
  // Probe on {rom_1_data_2[31:27], alu_1_flag_s}
  Comparator comparator_3 (
    .a({rom_1_data_2[31:27], alu_1_flag_s}), .b(rom_1_data_2[15:8]), .eq(comparator_3_eq));  // open: gt, lt

  // Notes on the sheet:
  //   contents of rom_1 (hex, n*v repeats v):
  //   41000000000200 41ff0000fe0501 41800000000602 41010000020003 417f0000fe0104 45000000000210
  //   45010000000611 45ff00007f0412 45800000400013 45020000010014 49000000010020 49ff0000000221
  //   497f0000800122 49fe0000ff0123 49010000020024 4d000000ff0130 4d010000000231 4d8000007f0032
  //   4dff0000fe0133 4d020000010034 51000000ff0140 51ff0000000241 518000007f0042 517f0000800143
  //   51550000aa0144 61000000000250 61ff0100000651 617f0100800152 61808000000653 610f0100100054
  //   65000000000660 65000100ff0161 658001007f0462 65010100000663 65ff0100fe0564 69000000000270
  //   6900ff00ff0171 6955aa00ff0172 69800100810173 697f00007f0074 6dffff00000280 6daa5500ff0181
  //   6d808000000282 6d010000010083 6d7fff00800184 71000004010090 71ff0004000691 717f0004800192
  //   71ffff04ff0593 71010104030094 75000004ff01a0 75010104ff01a1 750201040006a2 758001047e04a3
  //   75000104fe01a4 79ffff00ff01b0 7900ff000002b1 79aa55000002b2 79f00f000002b3 7980ff008001b4
  //   650000000006c0 650100000104c1 65000100ff01c2 658080000006c3 65ff0100fe05c4 ffffffffffffff
endmodule
